// Logisim project project DLD.circ as structural Verilog: 3 circuits, main circuit main
module main (
  input  in_1,
  input  in_2,
  input  in_3,
  input  a0,
  input  b0,
  input  a1,
  input  b1,
  input  a2,
  input  b2,
  input  a3,
  input  b3,
  output s0,
  output s1,
  output s2,
  output s3,
  output c4
);

  wire adder_1_cout, adder_2_cout, adder_3_cout, multiplexer_1_out, n2x4_decoder_1_a0_2, n2x4_decoder_1_a1_2,
       n2x4_decoder_1_a2, n2x4_decoder_1_a3, n2x4_decoder_2_a0_2, n2x4_decoder_2_a1_2, n2x4_decoder_2_a2,
       n2x4_decoder_2_a3, n7_segment_displayy_1_a_2, n7_segment_displayy_1_b_2, n7_segment_displayy_1_c_2,
       n7_segment_displayy_1_d_2, n7_segment_displayy_1_e, n7_segment_displayy_1_f, n7_segment_displayy_1_g,
       xor_1_out, xor_2_out, xor_3_out, xor_4_out;

  LED led_1 (.in(a0));
  LED led_2 (.in(b0));
  LED led_3 (.in(b1));
  LED led_4 (.in(b2));
  LED led_5 (.in(b3));
  LED led_6 (.in(a1));
  LED led_7 (.in(a2));
  LED led_8 (.in(a3));
  LED led_9 (.in(in_3));
  xor xor_1 (xor_1_out, b0, multiplexer_1_out);
  xor xor_2 (xor_2_out, b1, multiplexer_1_out);
  xor xor_3 (xor_3_out, b2, multiplexer_1_out);
  Multiplexer #(.enable("false")) multiplexer_1 (.in0(in_1), .in1(in_2), .out(multiplexer_1_out), .sel(in_3));
  xor xor_4 (xor_4_out, b3, multiplexer_1_out);
  LED led_10 (.in(s0));
  Adder #(.width(1)) adder_1 (.a(a0), .b(xor_1_out), .out(s0), .cin(multiplexer_1_out), .cout(adder_1_cout));
  LED led_11 (.in(s1));
  Adder #(.width(1)) adder_2 (.a(a1), .b(xor_2_out), .out(s1), .cin(adder_1_cout), .cout(adder_2_cout));
  LED led_12 (.in(s2));
  Adder #(.width(1)) adder_3 (.a(a2), .b(xor_3_out), .out(s2), .cin(adder_2_cout), .cout(adder_3_cout));
  LED led_13 (.in(s3));
  Adder #(.width(1)) adder_4 (.a(a3), .b(xor_4_out), .out(s3), .cin(adder_3_cout), .cout(c4));
  _2x4_decoder u_2x4_decoder_1 (
    .A0(s0), .A1(s1), .a0_2(n2x4_decoder_1_a0_2), .a1_2(n2x4_decoder_1_a1_2), .a2(n2x4_decoder_1_a2),
    .a3(n2x4_decoder_1_a3));
  _2x4_decoder u_2x4_decoder_2 (
    .A0(s2), .A1(s3), .a0_2(n2x4_decoder_2_a0_2), .a1_2(n2x4_decoder_2_a1_2), .a2(n2x4_decoder_2_a2),
    .a3(n2x4_decoder_2_a3));
  _7_segment_displayy u_7_segment_displayy_1 (
    .D(s0), .C(s1), .B(s2), .A(s3), .a_2(n7_segment_displayy_1_a_2), .b_2(n7_segment_displayy_1_b_2),
    .c_2(n7_segment_displayy_1_c_2), .d_2(n7_segment_displayy_1_d_2), .e(n7_segment_displayy_1_e),
    .f(n7_segment_displayy_1_f), .g(n7_segment_displayy_1_g));
  _7_Segment_Display u_7_segment_display_1 (
    .g(n7_segment_displayy_1_g), .f(n7_segment_displayy_1_f), .a(n7_segment_displayy_1_a_2),
    .b(n7_segment_displayy_1_b_2), .e(n7_segment_displayy_1_e), .d(n7_segment_displayy_1_d_2),
    .c(n7_segment_displayy_1_c_2));  // open: dp

  // Notes on the sheet:
  //   c0
  //   c1
  //   c2
  //   c3
endmodule

module _2x4_decoder (
  input  A0,
  input  A1,
  output a0_2,
  output a1_2,
  output a2,
  output a3
);

  wire not_1_out, not_2_out, not_3_out, not_4_out;

  and and_1 (a0_2, A0, A1);
  not not_1 (not_1_out, A1);
  not not_2 (not_2_out, A0);
  not not_3 (not_3_out, A0);
  not not_4 (not_4_out, A1);
  and and_2 (a1_2, A0, not_1_out);
  and and_3 (a2, not_2_out, A1);
  and and_4 (a3, not_3_out, not_4_out);
endmodule

module _7_segment_displayy (
  input  D,
  input  C,
  input  B,
  input  A,
  output a_2,
  output b_2,
  output c_2,
  output d_2,
  output e,
  output f,
  output g
);

  wire and_1_out, and_2_out, and_3_out, and_4_out, and_5_out, and_6_out, and_7_out, and_8_out, and_9_out,
       and_10_out, and_11_out, and_12_out, and_13_out, and_14_out, and_15_out, and_16_out, not_1_out,
       not_2_out, not_3_out, not_4_out, not_5_out, not_6_out, not_7_out, not_8_out, not_9_out, not_10_out,
       not_11_out, not_12_out, not_13_out, not_14_out, not_15_out, not_16_out, not_17_out, not_18_out,
       not_19_out, not_20_out, not_21_out;

  not not_1 (not_1_out, D);
  and and_1 (and_1_out, not_1_out, not_2_out);
  not not_2 (not_2_out, B);
  and and_2 (and_2_out, D, B);
  not not_3 (not_3_out, D);
  and and_3 (and_3_out, not_3_out, not_4_out);
  not not_4 (not_4_out, C);
  not not_5 (not_5_out, B);
  and and_4 (and_4_out, D, C);
  not not_6 (not_6_out, C);
  or or_1 (c_2, not_6_out, B, D);
  not not_7 (not_7_out, D);
  and and_5 (and_5_out, not_7_out, not_8_out);
  not not_8 (not_8_out, B);
  not not_9 (not_9_out, D);
  and and_6 (and_6_out, not_9_out, C);
  and and_7 (and_7_out, C, not_10_out);
  not not_10 (not_10_out, B);
  and and_8 (and_8_out, D, not_11_out, B);
  not not_11 (not_11_out, C);
  not not_12 (not_12_out, D);
  and and_9 (and_9_out, not_12_out, not_13_out);
  not not_13 (not_13_out, B);
  not not_14 (not_14_out, D);
  and and_10 (and_10_out, not_14_out, C);
  not not_15 (not_15_out, D);
  and and_11 (and_11_out, not_15_out, not_16_out);
  not not_16 (not_16_out, C);
  not not_17 (not_17_out, D);
  and and_12 (and_12_out, not_17_out, B);
  not not_18 (not_18_out, C);
  and and_13 (and_13_out, not_18_out, B);
  not not_19 (not_19_out, C);
  and and_14 (and_14_out, not_19_out, B);
  not not_20 (not_20_out, D);
  and and_15 (and_15_out, not_20_out, C);
  and and_16 (and_16_out, C, not_21_out);
  not not_21 (not_21_out, B);
  or or_2 (a_2, and_1_out, A, C, and_2_out);
  or or_3 (b_2, and_3_out, not_5_out, and_4_out);
  or or_4 (d_2, and_5_out, A, and_6_out, and_7_out, and_8_out);
  or or_5 (e, and_9_out, and_10_out);
  or or_6 (f, and_11_out, A, and_12_out, and_13_out);
  or or_7 (g, A, and_14_out, and_15_out, and_16_out);
endmodule
